# Fritzing sketch Murillo Fritzing (saved by Fritzing 0.9.3b)
breadboards: 1

parts:
  IC1 = L293D [package=THT]
  Componente1 = Arduino Uno (Rev3)
  M1 = DC Motor
  M2 = DC Motor
  M3 = DC Motor
  M4 = DC Motor
  IC2 = L293D [package=THT]
  VCC1 = 4 x AAA Battery Mount  # not connected
  VCC2 = 4 x AAA Battery Mount  # not connected

nets:
  N1: IC1.Enable_1, IC1.Enable_2, IC1.+V, Componente1.5V, IC2.Enable_1, IC2.Enable_2, IC2.+V
  N2: IC1.In_1, Componente1.D6_PWM
  N3: IC1.Out_1_(_Controlled_by_Enable_1_), M2.pin_2
  N4: IC1.0V, Componente1.GND, IC2.0V
  N5: IC1.Out_2_(_Controlled_by_Enable_1_), M2.pin_1
  N6: IC1.In_2, Componente1.D7
  N7: IC1.+Vmotor, Componente1.VIN, IC2.+Vmotor
  N8: IC1.In_3, Componente1.D4
  N9: IC1.Out_3_(_Controlled_by_Enable_2_), M1.pin_2
  N10: IC1.Out_4_(_Controlled_by_Enable_2_), M1.pin_1
  N11: IC1.In_4, Componente1.D3_PWM
  N12: Componente1.D8, IC2.In_4
  N13: Componente1.D9_PWM, IC2.In_3
  N14: Componente1.D11_PWM/MOSI, IC2.In_2
  N15: Componente1.D12/MISO, IC2.In_1
  N16: M3.pin_1, IC2.Out_1_(_Controlled_by_Enable_1_)
  N17: M3.pin_2, IC2.Out_2_(_Controlled_by_Enable_1_)
  N18: M4.pin_1, IC2.Out_4_(_Controlled_by_Enable_2_)
  N19: M4.pin_2, IC2.Out_3_(_Controlled_by_Enable_2_)
